// Logisim project B1_Group6_ALU_Design.circ as structural Verilog: 1 circuit, main circuit main
module main (
  input  CS2,
  input  CS1,
  input  CS0,
  input  B3,
  input  B2,
  input  B1,
  input  B0,
  input  A3,
  input  A2,
  input  A1,
  input  A0,
  input  in_12,
  output Sign_Flag,
  output Zero_Flag,
  output OverFlow,
  output Carry_Flag,
  output S3,
  output S2,
  output S1,
  output S0
);

  wire main_1_p2, n7404_1_p2, n7404_1_p4, n7404_1_p6, n7404_1_p7, n7404_1_p8, n7404_1_p9, n7408_1_p3,
       n7408_1_p6, n7408_1_p7, n7408_1_p8, n7408_1_p9, n7408_1_p12, n7408_2_p3, n7408_2_p6, n7408_2_p9,
       n7408_2_p12, n7408_3_p6, n7432_2_p3, n7432_2_p6, n7486_1_p3, n7486_1_p6, n7486_1_p9, n7486_1_p12,
       n7486_2_p1, n74157_1_p1, n74157_1_p2, n74157_1_p3, n74157_1_p5, n74157_1_p6, n74157_1_p9,
       n74157_1_p10, n74157_1_p12, n74157_1_p13;

  // _74157 74157_1: pin names not known; wires that end beside it: n74157_1_p1, n74157_1_p2, n74157_1_p3, S0, n74157_1_p5, n74157_1_p6, S1, in_12, n74157_1_p9, n74157_1_p10, S3, n74157_1_p12, n74157_1_p13, S2
  // _7404 7404_1: pin names not known; wires that end beside it: CS2, n7404_1_p2, CS1, n7404_1_p4, CS0, n7404_1_p6, n7404_1_p7, n7404_1_p8, n7404_1_p9, Zero_Flag, n7404_1_p2, n7404_1_p4, n7404_1_p6
  // _7408 7408_1: pin names not known; wires that end beside it: n7404_1_p2, CS0, n7408_1_p3, n7408_1_p3, CS1, n7408_1_p6, n7408_1_p7, n7408_1_p8, n7408_1_p9, CS2, n7404_1_p4, n7408_1_p12
  // _7486 7486_1: pin names not known; wires that end beside it: A0, n7408_1_p6, n7486_1_p3, A1, n7408_1_p6, n7486_1_p6, A3, n7408_1_p6, n7486_1_p9, A2, n7408_1_p6, n7486_1_p12
  // _7432 7432_1: pin names not known; wires that end beside it: n7404_1_p4, n7408_1_p3, n7408_1_p8, CS2, CS0, n7408_1_p7, n7408_1_p8, CS0, n74157_1_p1, n7408_1_p12, n7408_1_p6, n7404_1_p7, n7408_1_p8
  // _7408 7408_2: pin names not known; wires that end beside it: n7404_1_p8, B0, n7408_2_p3, n7404_1_p8, B1, n7408_2_p6, n7404_1_p8, B2, n7408_2_p9, n7404_1_p8, B3, n7408_2_p12
  // adderseparate_main main_1: pin names not known; wires that end beside it: n7486_1_p6, main_1_p2, 1'b1, n74157_1_p2, 1'b0, 1'b0, n7408_2_p6, n74157_1_p6, n74157_1_p5, n7408_1_p9, n7408_2_p3, n7486_1_p3, n74157_1_p3
  // _7486 7486_2: pin names not known; wires that end beside it: n7486_2_p1, Carry_Flag, OverFlow
  // _7408 7408_3: pin names not known; wires that end beside it: n74157_1_p2, n7408_1_p8, main_1_p2, n74157_1_p5, n7408_1_p8, n7408_3_p6, n7408_1_p8, n74157_1_p9, Carry_Flag, n7408_1_p8, n74157_1_p12, n7486_2_p1
  // _7432 7432_2: pin names not known; wires that end beside it: S3, S2, n7432_2_p3, n7432_2_p3, S1, n7432_2_p6, S0, n7432_2_p6, n7404_1_p9
  // adderseparate_main main_2: pin names not known; wires that end beside it: n7486_1_p9, n7486_2_p1, 1'b1, n74157_1_p12, 1'b0, 1'b0, n7408_2_p12, n74157_1_p10, n74157_1_p9, n7408_3_p6, n7408_2_p9, n7486_1_p12, n74157_1_p13

  assign Sign_Flag = S3;

  // Notes on the sheet:
  //   CS2'''''
  //   CS1'''
  //   CS0'''
  //   X
  //   C0
  //   A/L
  //   Z
endmodule
